# Fritzing sketch Wiring (saved by Fritzing 0.9.3b)
breadboards: 2

parts:
  Part1 = BME280 Breakout  # not connected
  Raspberry_Pi1 = Raspberry Pi B rev2
  U1 = LCD-16X2 [package=lcd-16x2_noholes]  # not connected
  U3 = mystery part, 4 pins [chip_label=I2C]
  Power_plug1 = Power plug
  Q1 = Basic FET P-Channel [package="D2Pak [SMD]"]
  R1 = Resistor [tolerance=±5% resistance=220 package="0402 [SMD]"]
  S1 = Momentary Switch [package=ksa_sealed_tac_switch]
  S2 = Momentary Switch [package=ksa_sealed_tac_switch]

nets:
  N1: Raspberry_Pi1.3V3, S1.3, S2.1
  N2: Raspberry_Pi1.5V, U3.pin1
  N3: Raspberry_Pi1.GPIO_2, U3.pin3
  N4: Raspberry_Pi1.GPIO_3, U3.pin4
  GND: Raspberry_Pi1.GND, U3.pin2, Power_plug1.GND, Q1.drain
  N5: Raspberry_Pi1.GPIO_17, Q1.Gate
  N6: Raspberry_Pi1.GPIO_27, S1.4
  N7: Raspberry_Pi1.GPIO_22, S2.2
  N8: Power_plug1.VCC, R1.Pin_1
  N9: Q1.source, R1.Pin_0

notes:
  12V
  HEAT
