# Fritzing sketch incubator (saved by Fritzing 0.9.3b)
breadboards: 1

parts:
  Raspberry_Pi1 = Raspberry Pi B rev2
  Temp_Sensor = BME280 Breakout  # not connected
  U1 = mystery part, 12 pins [chip_label=DRV8835]  # not connected
  M1 = DC Motor
  J1 = Power Jack [package=power_jack_slot]
  R1 = Resistor [tolerance=±5% resistance=10 package=THT]
  R2 = Resistor [tolerance=±5% resistance=10 package=THT]
  R3 = Resistor [tolerance=±5% resistance=10 package=THT]
  LED1 = LED - 5mm [color="Red (633nm)" package="5 mm [THT]"]
  S1 = Momentary Switch [package=tactile-pth]
  S2 = Momentary Switch [package=tactile-pth]
  R4 = Resistor [tolerance=±5% resistance=220 package="2512 [SMD]"]

nets:
  N1: Raspberry_Pi1.3V3, S1.2, S2.2
  N2: Raspberry_Pi1.5V, M1.pin_1
  GND: Raspberry_Pi1.GND, M1.pin_2, J1.GND, R4.Pin_0
  N3: Raspberry_Pi1.GPIO_27, S2.1
  N4: Raspberry_Pi1.GPIO_4, LED1.anode
  N5: R1.Pin_0, R2.Pin_0, R3.Pin_0
  N6: R1.Pin_1, R2.Pin_1, R3.Pin_1
  N7: LED1.cathode, R4.Pin_1

notes:
  9V DC
  Cement Resistor
  10W 10ohm
  ADD HEATSINK!
  25mm Fan
  5V 0.05A
  I2C 16x2 LCD
  RED STRIPE 5V
  BLACK GND
  GREEN SDA
  YELLOW SCL
